// Logisim project nanoprojeto_estufa.circ as structural Verilog: 9 circuits, main circuit main
module main (
  input  [7:0] pH__canaletas,
  input  [7:0] pH__adubo,
  input  [7:0] \iluminação ,
  input  [7:0] temperatura,
  input  [7:0] \pressão ,
  output \Bomba_Secundária ,
  output Bomba_Central,
  output Aquecedor,
  output \Lâmpadas ,
  output Ventiladores
);

  wire manometer_comparator_1_menor_igual, phmeter_4to6_comparator_1_maior, phmeter_4to6_comparator_1_menor;

  PHMETER_4to6_comparator phmeter_4to6_comparator_1 (
    .entrada_s2c(pH__canaletas), .maior(phmeter_4to6_comparator_1_maior),
    .menor(phmeter_4to6_comparator_1_menor));  // open: aceitavel
  PHMETER_aprox2_comparator phmeter_aprox2_comparator_1 (
    .entrada_sc2(pH__adubo), .menor(\Bomba_Secundária ));  // open: maior, aceitavel
  CENTRAL_PUMP_controller central_pump_controller_1 (
    .low_pressure(manometer_comparator_1_menor_igual), .high_temperature(Ventiladores),
    .low_pH(phmeter_4to6_comparator_1_menor), .high_pH(phmeter_4to6_comparator_1_maior), .I_O(Bomba_Central));
  LUXMETER_comparator luxmeter_comparator_1 (
    .entrada(\iluminação ), .menor_igual(\Lâmpadas ));  // open: maior_igual, aceitavel
  THERMOSTAT_comparator thermostat_comparator_1 (
    .entrada_sc2(temperatura), .maior_igual(Ventiladores), .menor_igual(Aquecedor));  // open: aceitavel
  MANOMETER_comparator manometer_comparator_1 (
    .entrada(\pressão ), .menor_igual(manometer_comparator_1_menor_igual));  // open: maior_igual, aceitavel

  // Notes on the sheet:
  //   (s2c)
  //   (s2c)
  //   Entradas do circuito:
  //   (s2c)
endmodule

module PHMETER_4to6_comparator (
  input  [7:0] entrada_s2c,
  output maior,
  output aceitavel,
  output menor
);

  wire comparator_1_eq, comparator_1_lt, comparator_2_eq, comparator_2_gt, or_1_out, or_2_out;

  Comparator comparator_1 (.a(entrada_s2c), .b(8'hd5), .gt(maior), .eq(comparator_1_eq), .lt(comparator_1_lt));
  Comparator comparator_2 (.a(entrada_s2c), .b(8'hb3), .gt(comparator_2_gt), .eq(comparator_2_eq), .lt(menor));
  or or_1 (or_1_out, comparator_1_eq, comparator_1_lt);
  or or_2 (or_2_out, comparator_2_gt, comparator_2_eq);
  and and_1 (aceitavel, or_1_out, or_2_out);

  // Notes on the sheet:
  //   -43 ref
  //   -77 ref
  //   O circuito recebe a saída do sensor de pH com 8 bits em complemento de 2 (-128 até 127) que representam o pH (0 até 14) e verifica se o pH está entre 4 e 6, caso não esteja a saída é 0 e caso esteja a saída é 1.
endmodule

module THERMOSTAT_comparator (
  input  [7:0] entrada_sc2,
  output maior_igual,
  output aceitavel,
  output menor_igual
);

  wire comparator_1_eq, comparator_1_gt, comparator_1_lt, comparator_2_eq, comparator_2_gt, comparator_2_lt;

  Comparator comparator_1 (
    .a(entrada_sc2), .b(8'h3f), .gt(comparator_1_gt), .eq(comparator_1_eq), .lt(comparator_1_lt));
  Comparator comparator_2 (
    .a(entrada_sc2), .b(8'h19), .gt(comparator_2_gt), .eq(comparator_2_eq), .lt(comparator_2_lt));
  or or_1 (maior_igual, comparator_1_gt, comparator_1_eq);
  or or_2 (menor_igual, comparator_2_eq, comparator_2_lt);
  and and_1 (aceitavel, comparator_1_lt, comparator_2_gt);

  // Notes on the sheet:
  //   63 ref
  //   25 ref
  //   Recebe a saída do sensor de temperatura em 8 bits (-128 até 127) que representam (-50 celsius até +50 celsius) e tem saída 1 se a temperatura estiver entre 10 celsius e 25 celsius.
endmodule

module PHMETER_aprox2_comparator (
  input  [7:0] entrada_sc2,
  output maior,
  output aceitavel,
  output menor
);

  wire comparator_1_eq, comparator_1_lt, comparator_2_eq, comparator_2_gt, or_1_out, or_2_out;

  Comparator comparator_1 (.a(entrada_sc2), .b(8'ha), .gt(maior), .eq(comparator_1_eq), .lt(comparator_1_lt));
  Comparator comparator_2 (.a(entrada_sc2), .b(8'hf6), .gt(comparator_2_gt), .eq(comparator_2_eq), .lt(menor));
  or or_1 (or_1_out, comparator_1_eq, comparator_1_lt);
  or or_2 (or_2_out, comparator_2_gt, comparator_2_eq);
  and and_1 (aceitavel, or_1_out, or_2_out);

  // Notes on the sheet:
  //   +10 ref
  //   -10 ref
  //   Verífica se o pH está próximo de 2
endmodule

module MANOMETER_comparator (
  input  [7:0] entrada,
  output maior_igual,
  output aceitavel,
  output menor_igual
);

  wire comparator_1_eq, comparator_1_gt, comparator_1_lt, comparator_2_eq, comparator_2_gt, comparator_2_lt;

  Comparator #(.mode("unsigned")) comparator_1 (
    .a(entrada), .b(8'h66), .gt(comparator_1_gt), .eq(comparator_1_eq), .lt(comparator_1_lt));
  Comparator #(.mode("unsigned")) comparator_2 (
    .a(entrada), .b(8'h33), .gt(comparator_2_gt), .eq(comparator_2_eq), .lt(comparator_2_lt));
  or or_1 (maior_igual, comparator_1_gt, comparator_1_eq);
  or or_2 (menor_igual, comparator_2_eq, comparator_2_lt);
  and and_1 (aceitavel, comparator_1_lt, comparator_2_gt);

  // Notes on the sheet:
  //   102 ref
  //   51 ref
  //   Recebe a saída do sensor de pressão d'água em um byte (0 até 255) que representam (0% até 100%) e tem saída 1 se a pressão estiver entre 20% e 40%;
endmodule

module DISPLAY_decoder (
  input  [3:0] in_1,
  output e,
  output g,
  output c,
  output f,
  output b,
  output d,
  output a
);

  wire and_1_out, and_2_out, and_3_out, and_4_out, and_5_out, and_6_out, and_7_out, and_8_out, and_9_out,
       and_10_out, and_11_out, and_12_out, and_13_out, and_14_out, and_15_out, and_16_out, and_17_out,
       and_18_out, and_19_out, and_20_out, and_21_out, and_22_out, and_23_out, and_24_out, and_25_out,
       and_26_out, and_27_out, and_28_out, nand_1_out, nor_1_out, nor_2_out, nor_3_out, nor_4_out, nor_5_out,
       or_1_out, or_2_out, or_4_out, or_5_out, or_7_out, or_8_out, or_9_out, or_11_out, or_12_out, or_13_out,
       or_14_out, or_15_out, or_17_out, or_18_out, or_20_out, or_21_out, or_23_out, or_24_out;

  and and_1 (and_1_out, in_1[2], in_1[1]);
  and and_2 (and_2_out, in_1[3], ~in_1[2]);  // AND_Gate
  and and_3 (and_3_out, and_2_out, ~in_1[1]);  // AND_Gate
  or or_1 (or_1_out, and_1_out, and_3_out);
  and and_4 (and_4_out, ~in_1[3], in_1[2]);  // AND_Gate
  and and_5 (and_5_out, and_4_out, in_1[0]);
  or or_2 (or_2_out, or_1_out, or_4_out);
  or or_3 (a, or_2_out, nor_1_out);
  and and_6 (and_6_out, ~in_1[3], in_1[1]);  // AND_Gate
  or or_4 (or_4_out, and_5_out, and_6_out);
  nor nor_1 (nor_1_out, in_1[0], in_1[2]);
  and and_7 (and_7_out, ~in_1[1], in_1[0]);  // AND_Gate
  and and_8 (and_8_out, in_1[3], and_7_out);
  or or_5 (or_5_out, and_8_out, nor_2_out);
  or or_6 (b, or_5_out, and_9_out);
  nor nor_2 (nor_2_out, in_1[2], in_1[0]);
  and and_9 (and_9_out, ~in_1[3], or_8_out);  // AND_Gate
  and and_10 (and_10_out, in_1[1], in_1[0]);
  nor nor_3 (nor_3_out, in_1[1], in_1[0]);
  or or_7 (or_7_out, and_10_out, nor_3_out);
  or or_8 (or_8_out, ~in_1[2], or_7_out);  // OR_Gate
  and and_11 (and_11_out, ~in_1[3], in_1[2]);  // AND_Gate
  and and_12 (and_12_out, in_1[0], ~in_1[1]);  // AND_Gate
  or or_9 (or_9_out, and_11_out, and_12_out);
  or or_10 (c, or_9_out, and_13_out);
  or or_11 (or_11_out, ~in_1[1], in_1[0]);  // OR_Gate
  or or_12 (or_12_out, in_1[3], or_11_out);
  and and_13 (and_13_out, ~in_1[2], or_12_out);  // AND_Gate
  and and_14 (and_14_out, in_1[3], in_1[2]);
  and and_15 (and_15_out, ~in_1[3], in_1[1]);  // AND_Gate
  or or_13 (or_13_out, and_14_out, and_15_out);
  or or_14 (or_14_out, or_13_out, nor_4_out);
  and and_16 (and_16_out, or_14_out, ~in_1[0]);  // AND_Gate
  and and_17 (and_17_out, ~in_1[1], in_1[2]);  // AND_Gate
  nor nor_4 (nor_4_out, in_1[2], in_1[1]);
  or or_15 (or_15_out, and_17_out, and_19_out);
  and and_18 (and_18_out, in_1[0], or_15_out);
  or or_16 (d, and_16_out, and_18_out);
  and and_19 (and_19_out, in_1[1], ~in_1[2]);  // AND_Gate
  or or_17 (or_17_out, in_1[2], in_1[1]);
  and and_20 (and_20_out, in_1[3], or_17_out);
  or or_18 (or_18_out, ~in_1[2], in_1[1]);  // OR_Gate
  or or_19 (e, and_20_out, and_21_out);
  and and_21 (and_21_out, or_18_out, ~in_1[0]);  // AND_Gate
  and and_22 (and_22_out, ~in_1[3], in_1[2]);  // AND_Gate
  and and_23 (and_23_out, and_22_out, ~in_1[1]);  // AND_Gate
  or or_20 (or_20_out, ~in_1[2], in_1[1]);  // OR_Gate
  and and_24 (and_24_out, in_1[3], or_20_out);
  or or_21 (or_21_out, and_23_out, and_24_out);
  or or_22 (f, or_21_out, and_26_out);
  and and_25 (and_25_out, in_1[1], in_1[2]);
  or or_23 (or_23_out, and_25_out, nor_5_out);
  and and_26 (and_26_out, ~in_1[0], or_23_out);  // AND_Gate
  nor nor_5 (nor_5_out, in_1[2], in_1[1]);
  or or_24 (or_24_out, in_1[3], and_27_out);
  and and_27 (and_27_out, in_1[2], ~in_1[1]);  // AND_Gate
  or or_25 (g, or_24_out, and_28_out);
  nand nand_1 (nand_1_out, in_1[2], in_1[0]);
  and and_28 (and_28_out, in_1[1], nand_1_out);
endmodule

module LUXMETER_comparator (
  input  [7:0] entrada,
  output maior_igual,
  output aceitavel,
  output menor_igual
);

  wire comparator_1_eq, comparator_1_gt, comparator_1_lt, comparator_2_eq, comparator_2_gt, comparator_2_lt;

  Comparator #(.mode("unsigned")) comparator_1 (
    .a(entrada), .b(8'hb2), .gt(comparator_1_gt), .eq(comparator_1_eq), .lt(comparator_1_lt));
  Comparator #(.mode("unsigned")) comparator_2 (
    .a(entrada), .b(8'h7f), .gt(comparator_2_gt), .eq(comparator_2_eq), .lt(comparator_2_lt));
  or or_1 (maior_igual, comparator_1_gt, comparator_1_eq);
  or or_2 (menor_igual, comparator_2_eq, comparator_2_lt);
  and and_1 (aceitavel, comparator_1_lt, comparator_2_gt);

  // Notes on the sheet:
  //   178 ref
  //   127  ref
  //   Recebe a saída do sensor de iluminação em um byte (0 até 255) que representam (0 cd/m^2 até 100 cd/m^2) e tem saída 1 se a iluminação estiver entre 50 e 70 candelas por metro quadrado;
endmodule

module test (
  input  [7:0] in_1,
  input  [7:0] in_2,
  input  [7:0] in_3,
  input  [7:0] in_4,
  input  [3:0] in_5
);

  wire display_decoder_1_a, display_decoder_1_b, display_decoder_1_c, display_decoder_1_d,
       display_decoder_1_e, display_decoder_1_f, display_decoder_1_g;

  _7_Segment_Display u_7_segment_display_1 (
    .g(display_decoder_1_g), .f(display_decoder_1_f), .a(display_decoder_1_a), .b(display_decoder_1_b),
    .e(display_decoder_1_e), .d(display_decoder_1_d), .c(display_decoder_1_c));  // open: dp
  LUXMETER_comparator luxmeter_comparator_1 (.entrada(in_4));  // open: maior_igual, aceitavel, menor_igual
  DISPLAY_decoder display_decoder_1 (
    .a(display_decoder_1_a), .b(display_decoder_1_b), .c(display_decoder_1_c), .d(display_decoder_1_d),
    .e(display_decoder_1_e), .f(display_decoder_1_f), .g(display_decoder_1_g), .in_1(in_5));
  PHMETER_aprox2_comparator phmeter_aprox2_comparator_1 (.entrada_sc2(in_1));  // open: maior, aceitavel, menor
  PHMETER_4to6_comparator phmeter_4to6_comparator_1 (.entrada_s2c(in_1));  // open: aceitavel, maior, menor
  THERMOSTAT_comparator thermostat_comparator_1 (.entrada_sc2(in_2));  // open: aceitavel, maior_igual, menor_igual
  MANOMETER_comparator manometer_comparator_1 (.entrada(in_3));  // open: maior_igual, aceitavel, menor_igual
endmodule

module CENTRAL_PUMP_controller (
  input  low_pressure,
  input  high_temperature,
  input  low_pH,
  input  high_pH,
  output I_O
);

  wire or_1_out, or_2_out;

  and and_1 (I_O, low_pressure, or_1_out);
  or or_1 (or_1_out, high_temperature, or_2_out);
  or or_2 (or_2_out, low_pH, high_pH);

  // Notes on the sheet:
  //   pressure<20%
  //   A
  //   Controle da bomba central
  //   temperature>25°C
  //   B
  //    pH<4
  //   C
  //   pH>6
  //   D
endmodule
